# Fritzing sketch Gravity Car (saved by Fritzing 0.9.3b)
breadboards: 1

parts:
  Componente1 = Arduino Uno (Rev3) - ICSP
  U1 = POT [package=pot_alpha_rv16af-20]
  U2 = POT [package=pot_alpha_rv16af-20]
  U3 = POT [package=pot_alpha_rv16af-20]
  Componente2 = Bluetooth HC-05 Macho
  R1 = Resistor [tolerance=±5% resistance=680 package=THT]
  R2 = Resistor [tolerance=±5% resistance=470 package=THT]

nets:
  N1: Componente1.A0, U3.S
  N2: Componente1.A1, U2.S
  N3: Componente1.A2, U1.S
  N4: Componente1.D0/RX, Componente2.TXD
  N5: Componente1.D1/TX, R2.Pin_0
  5V: Componente1.5V, U1.E, U2.E, U3.E, Componente2.VCC
  GND: Componente1.GND, U1.A, U2.A, U3.A, Componente2.GND, R1.Pin_1
  N6: Componente2.RXD, R1.Pin_0, R2.Pin_1
